// Digital circuit hazard-unit.dig as structural Verilog
module hazard_unit (
  input  [4:0] WR_4,
  input  RFW_4,
  input  [4:0] WR_3,
  input  RFW_3,
  input  PCbr_2,
  input  CLR,
  input  MR_3,
  input  [4:0] RR0_2,
  input  [4:0] RR1_2,
  output [1:0] FWDRS1,
  output [1:0] FWDRS2,
  output FLUSH,
  output STALL,
  output nSTALL
);

  wire and_1_out, and_2_out, and_3_out, and_4_out, and_5_out, and_6_out, comparator_1_eq, comparator_2_eq,
       comparator_3_eq, comparator_4_eq, comparator_5_eq, comparator_6_eq;

  Comparator #(.Bits(5)) comparator_1 (.a(RR0_2), .b(WR_4), .eq(comparator_1_eq));  // open: gt, lt
  Comparator #(.Bits(5)) comparator_2 (.a(RR0_2), .b(WR_3), .eq(comparator_2_eq));  // open: gt, lt
  Comparator #(.Bits(5)) comparator_3 (.a(RR1_2), .b(WR_4), .eq(comparator_3_eq));  // open: gt, lt
  Comparator #(.Bits(5)) comparator_4 (.a(RR1_2), .b(WR_3), .eq(comparator_4_eq));  // open: gt, lt
  Comparator #(.Bits(5)) comparator_5 (.a(RR0_2), .b(WR_3), .eq(comparator_5_eq));  // open: gt, lt
  Comparator #(.Bits(5)) comparator_6 (.a(RR1_2), .b(WR_3), .eq(comparator_6_eq));  // open: gt, lt
  or or_1 (FLUSH, PCbr_2, CLR);
  and and_1 (and_1_out, comparator_1_eq, RFW_4);
  and and_2 (and_2_out, comparator_2_eq, RFW_3);
  and and_3 (and_3_out, comparator_3_eq, RFW_4);
  and and_4 (and_4_out, comparator_4_eq, RFW_3);
  and and_5 (and_5_out, comparator_5_eq, MR_3);
  and and_6 (and_6_out, comparator_6_eq, MR_3);
  or or_2 (STALL, and_5_out, and_6_out);
  PriorityEncoder #(.Selector_Bits(2)) RS1 (
    .in0(1'b1), .in1(and_1_out), .in2(and_2_out), .in3(1'b0), .num(FWDRS1));  // open: any
  PriorityEncoder #(.Selector_Bits(2)) RS2 (
    .in0(1'b1), .in1(and_3_out), .in2(and_4_out), .in3(1'b0), .num(FWDRS2));  // open: any
  not not_1 (nSTALL, STALL);
endmodule
